// Logisim project backup.circ as structural Verilog: 3 circuits, main circuit main
module main (
);

  wire clk, comparator_1_eq, M_ULA, WE_BR, WE_ME;
  wire [1:0] M_IMM, PC_OP, SAVE;
  wire [2:0] funct;
  wire [3:0] multiplexer_3_out, rb4b;
  wire [7:4] rom_1_data_2;
  wire [11:0] adder_2_out, adder_3_out, bit_extender_1_out, dado, endM, IMM, multiplexer_1_out,
       multiplexer_2_out, multiplexer_4_out, multiplexer_5_out, pc_m1, ram_1_dout, register_1_q, ula_1_s;
  wire [11:8] rom_1_data;
  wire [15:12] rom_2_data;

  Clock clock_1 (.out(clk));
  Adder #(.width(12)) adder_1 (.a(register_1_q), .b(12'h1), .out(pc_m1));  // open: cin, cout
  Adder #(.width(12)) adder_2 (.a(register_1_q), .b(IMM), .out(adder_2_out));  // open: cin, cout
  // Probe on dado
  Comparator #(.width(12)) comparator_1 (.a(dado), .b({12{1'b0}}), .eq(comparator_1_eq));  // open: gt, lt
  assign bit_extender_1_out = {{8{1'b0}}, rb4b};  // Bit_Extender bit_extender_1
  Multiplexer #(.width(12)) multiplexer_1 (
    .in0(pc_m1), .in1(adder_3_out), .out(multiplexer_1_out), .sel(comparator_1_eq));
  Adder #(.width(12)) adder_3 (.a(pc_m1), .b(bit_extender_1_out), .out(adder_3_out));  // open: cin, cout
  Register #(.width(12)) register_1 (.D(multiplexer_2_out), .en(1'b1), .clk(clk), .Q(register_1_q));  // open: clr
  Multiplexer #(.select(2), .width(12)) multiplexer_2 (
    .in0(pc_m1), .in1(adder_2_out), .in2(multiplexer_1_out), .out(multiplexer_2_out), .sel(PC_OP));  // open: in3
  // Probe on multiplexer_1_out
  ROM #(.addrWidth(12), .dataWidth(12)) rom_1 (.addr(register_1_q), .data({rom_1_data, rom_1_data_2, rb4b}));
  // Probe on rom_1_data
  // Probe on rom_1_data_2
  Multiplexer #(.select(2), .width(4)) multiplexer_3 (
    .in0(rom_1_data_2), .in1(4'b1111), .in2(4'b0001), .out(multiplexer_3_out), .sel(M_IMM));  // open: in3
  // Probe on multiplexer_5_out
  assign IMM = {{4{rom_1_data_2[7]}}, {rom_1_data_2, rb4b}};  // Bit_Extender bit_extender_2
  ROM #(.addrWidth(4), .dataWidth(16)) rom_2 (
    .addr(rom_1_data), .data({rom_2_data, M_IMM, M_ULA, WE_BR, funct, SAVE, WE_ME, PC_OP}));
  banco_de_registradores banco_de_registradores_1 (
    .Dado(multiplexer_5_out), .WE(WE_BR), .RD(multiplexer_3_out), .clock(clk), .RA(multiplexer_3_out),
    .RB(rb4b), .RS1(dado), .RS2(endM));
  // Probe on endM
  // Probe on IMM
  Multiplexer #(.width(12)) multiplexer_4 (.in0(endM), .in1(IMM), .out(multiplexer_4_out), .sel(M_ULA));
  // Probe on funct
  // Probe on SAVE
  Multiplexer #(.select(2), .width(12)) multiplexer_5 (
    .in0(ram_1_dout), .in1(ula_1_s), .in2(pc_m1), .out(multiplexer_5_out), .sel(SAVE));  // open: in3
  ULA ula_1 (.A(dado), .B(multiplexer_4_out), .funct(funct), .S(ula_1_s));
  // Probe on dado
  RAM #(.addrWidth(12), .dataWidth(12)) ram_1 (
    .addr(endM), .we(WE_ME), .oe(1'b1), .clk(clk), .din(dado), .dout(ram_1_dout));

  // Other names for the same wires on the sheet: ra[11:0] = dado

  // Notes on the sheet:
  //   contents of rom_1 (hex, n*v repeats v):
  //   604 2f 2f0 601 3f 922 123 afe
  //   contents of rom_2 (hex, n*v repeats v):
  //   108 1128 2148 3168 4188 51a8 6708 7100 810c 900a a911
endmodule

module banco_de_registradores (
  input  [11:0] Dado,
  input  WE,
  input  [3:0] RD,
  input  clock,
  input  [3:0] RA,
  input  [3:0] RB,
  output [11:0] RS1,
  output [11:0] RS2
);

  wire Er1, Er2, Er3, Er4, Er5, Er6, Er7, Er8, Er9, Er10, Er11, Er12, Er13, Er14, Er15, Er16;
  wire [11:0] register_1_q, register_2_q, register_3_q, register_4_q, register_5_q, register_6_q,
       register_7_q, register_8_q, register_9_q, register_10_q, register_11_q, register_12_q, register_13_q,
       register_14_q, register_15_q, register_16_q;

  Demultiplexer #(.enable("true"), .select(4)) demultiplexer_1 (
    .out0(Er1), .out1(Er2), .out2(Er3), .out3(Er4), .out4(Er5), .out5(Er6), .out6(Er7), .out7(Er8),
    .out8(Er9), .out9(Er10), .out10(Er11), .out11(Er12), .out12(Er13), .out13(Er14), .out14(Er15),
    .out15(Er16), .in(WE), .sel(RD));  // open: en
  Register #(.width(12)) register_1 (.D(Dado), .en(Er1), .clk(clock), .Q(register_1_q));  // open: clr
  Register #(.width(12)) register_2 (.D(Dado), .en(Er2), .clk(clock), .Q(register_2_q));  // open: clr
  Register #(.width(12)) register_3 (.D(Dado), .en(Er3), .clk(clock), .Q(register_3_q));  // open: clr
  Register #(.width(12)) register_4 (.D(Dado), .en(Er4), .clk(clock), .Q(register_4_q));  // open: clr
  Register #(.width(12)) register_5 (.D(Dado), .en(Er5), .clk(clock), .Q(register_5_q));  // open: clr
  Register #(.width(12)) register_6 (.D(Dado), .en(Er6), .clk(clock), .Q(register_6_q));  // open: clr
  Register #(.width(12)) register_7 (.D(Dado), .en(Er7), .clk(clock), .Q(register_7_q));  // open: clr
  Register #(.width(12)) register_8 (.D(Dado), .en(Er8), .clk(clock), .Q(register_8_q));  // open: clr
  Multiplexer #(.enable("true"), .select(4), .width(12)) multiplexer_1 (
    .in0(register_1_q), .in1(register_2_q), .in2(register_3_q), .in3(register_4_q), .in4(register_5_q),
    .in5(register_6_q), .in6(register_7_q), .in7(register_8_q), .in8(register_9_q), .in9(register_10_q),
    .in10(register_11_q), .in11(register_12_q), .in12(register_13_q), .in13(register_14_q),
    .in14(register_15_q), .in15(register_16_q), .out(RS1), .sel(RA));  // open: en
  Register #(.width(12)) register_9 (.D(Dado), .en(Er9), .clk(clock), .Q(register_9_q));  // open: clr
  Register #(.width(12)) register_10 (.D(Dado), .en(Er10), .clk(clock), .Q(register_10_q));  // open: clr
  Register #(.width(12)) register_11 (.D(Dado), .en(Er11), .clk(clock), .Q(register_11_q));  // open: clr
  Register #(.width(12)) register_12 (.D(Dado), .en(Er12), .clk(clock), .Q(register_12_q));  // open: clr
  Multiplexer #(.enable("true"), .select(4), .width(12)) multiplexer_2 (
    .in0(register_1_q), .in1(register_2_q), .in2(register_3_q), .in3(register_4_q), .in4(register_5_q),
    .in5(register_6_q), .in6(register_7_q), .in7(register_8_q), .in8(register_9_q), .in9(register_10_q),
    .in10(register_11_q), .in11(register_12_q), .in12(register_13_q), .in13(register_14_q),
    .in14(register_15_q), .in15(register_16_q), .out(RS2), .sel(RB));  // open: en
  Register #(.width(12)) register_13 (.D(Dado), .en(Er13), .clk(clock), .Q(register_13_q));  // open: clr
  Register #(.width(12)) register_14 (.D(Dado), .en(Er14), .clk(clock), .Q(register_14_q));  // open: clr
  Register #(.width(12)) register_15 (.D(Dado), .en(Er15), .clk(clock), .Q(register_15_q));  // open: clr
  Register #(.width(12)) register_16 (.D(Dado), .en(Er16), .clk(clock), .Q(register_16_q));  // open: clr
endmodule

module ULA (
  input  [11:0] A,
  input  [11:0] B,
  input  [2:0] funct,
  output [11:0] S
);

  wire [11:0] adder_1_out, and_1_out, divider_1_out, multiplier_1_out, or_1_out, subtractor_1_out;

  Adder #(.width(12)) adder_1 (.a(A), .b(B), .out(adder_1_out));  // open: cin, cout
  Subtractor #(.width(12)) subtractor_1 (.a(A), .b(B), .out(subtractor_1_out));  // open: bin, bout
  Multiplier #(.width(12)) multiplier_1 (.a(A), .b(B), .out(multiplier_1_out));  // open: cin, cout
  Divider #(.width(12)) divider_1 (.a(A), .b(B), .out(divider_1_out));  // open: upper, rem
  assign and_1_out = A & B;  // AND_Gate and_1, 12 bits wide
  assign or_1_out = A | B;  // OR_Gate or_1, 12 bits wide
  Multiplexer #(.enable("true"), .select(3), .width(12)) multiplexer_1 (
    .in0(adder_1_out), .in1(subtractor_1_out), .in2(multiplier_1_out), .in3(divider_1_out), .in4(and_1_out),
    .in5(or_1_out), .out(S), .sel(funct));  // open: in6, in7, en
endmodule
